// Logisim project Actual CPU.circ as structural Verilog: 2 circuits, main circuit main
module main (
  input  Manual_Clock,
  input  Clock_Select,
  input  Reset,
  output LUO,
  output LUS,
  output ROI,
  output IRO,
  output RBO,
  output IRI,
  output RBI,
  output RAO,
  output RAO_2,
  output RAI,
  output RAI_2,
  output ROO,
  output PCE,
  output MRI,
  output PCO,
  output PCI
);

  wire clock_1_out, decoder_1_out5, multiplexer_1_out, not_1_out, or_1_out;
  wire [2:0] adder_1_out, register_2_q;
  wire [3:0] adder_2_out, multiplexer_2_out, n7_segment_rom_1_out_2, n7_segment_rom_1_out_2_2,
       n7_segment_rom_1_out_3, n7_segment_rom_1_out_3_2, n7_segment_rom_1_out_4, n7_segment_rom_1_out_4_2,
       ram_1_data, ram_1_data_2, register_1_q, register_1_q_2, register_3_q, register_6_q, register_6_q_2,
       register_7_q, undriven;
  wire [7:0] adder_3_out, register_4_q, register_5_q, rom_1_data, subtractor_1_out;
  wire [16:16] rom_2_data;

  // Probe on {rom_2_data[16], LUO, LUS, IRO, IRI, RAO, RAI, ROO, MRI, ROI, RBO, RBI, RAO_2, RAI_2, PCE, PCO, PCI}
  Register register_1 (
    .D({ram_1_data_2, ram_1_data}), .en(IRI), .Q({register_1_q, register_1_q_2}), .clk(multiplexer_1_out),
    .clr(Reset));
  Adder #(.width(3)) adder_1 (.a(register_2_q), .b(3'b001), .out(adder_1_out));  // open: cin, cout
  Register #(.width(3)) register_2 (.D(adder_1_out), .en(1'b1), .Q(register_2_q), .clk(not_1_out), .clr(or_1_out));
  Register #(.width(4)) register_3 (.D(ram_1_data), .en(MRI), .Q(register_3_q), .clk(multiplexer_1_out), .clr(Reset));
  RAM #(.addrWidth(4), .bus("separate")) ram_1 (
    .addr(register_3_q), .din({ram_1_data_2, ram_1_data}), .data({ram_1_data_2, ram_1_data}), .str(RAI),
    .sel(1'b1), .clk(multiplexer_1_out), .ld(RAO), .clr(Reset));
  ROM #(.addrWidth(4)) rom_1 (.addr(register_3_q), .data(rom_1_data), .sel(1'b1));
  assign {ram_1_data_2, ram_1_data} = ROO ? rom_1_data : 8'bz;  // Controlled_Buffer controlled_buffer_1
  assign {ram_1_data_2, ram_1_data} = IRO ? {undriven, register_1_q_2} : 8'bz;  // Controlled_Buffer controlled_buffer_2
  Decoder #(.select(3), .enable("false")) decoder_1 (
    .out5(decoder_1_out5), .sel(register_2_q));  // open: out0, out1, out2, out3, out4, out6, out7
  not not_1 (not_1_out, multiplexer_1_out);
  Multiplexer #(.enable("false")) multiplexer_1 (
    .in0(Manual_Clock), .in1(clock_1_out), .out(multiplexer_1_out), .sel(Clock_Select));
  or or_1 (or_1_out, decoder_1_out5, rom_2_data[16], Reset);
  ROM #(.addrWidth(7), .dataWidth(17)) rom_2 (
    .addr({register_2_q, register_1_q}),
    .data({rom_2_data[16], LUO, LUS, IRO, IRI, RAO, RAI, ROO, MRI, ROI, RBO, RBI, RAO_2, RAI_2, PCE, PCO, PCI}),
    .sel(1'b1));
  // Probe on {ram_1_data_2, ram_1_data}
  Clock clock_1 (.out(clock_1_out));
  assign ram_1_data = PCO ? register_7_q : 4'bz;  // Controlled_Buffer controlled_buffer_3
  Multiplexer #(.width(4), .enable("false")) multiplexer_2 (
    .in0(adder_2_out), .in1(ram_1_data), .out(multiplexer_2_out), .sel(PCI));
  // Probe on multiplexer_2_out
  Register register_4 (
    .D({ram_1_data_2, ram_1_data}), .en(RAI_2), .Q(register_4_q), .clk(multiplexer_1_out), .clr(Reset));
  Register register_5 (
    .D({ram_1_data_2, ram_1_data}), .en(RBI), .Q(register_5_q), .clk(multiplexer_1_out), .clr(Reset));
  Register register_6 (
    .D({ram_1_data_2, ram_1_data}), .en(ROI), .Q({register_6_q_2, register_6_q}), .clk(multiplexer_1_out),
    .clr(Reset));
  Pull_Resistor pull_resistor_1 (.node({ram_1_data_2, ram_1_data}));
  Adder #(.width(4)) adder_2 (.a(4'b0001), .b(register_7_q), .out(adder_2_out));  // open: cin, cout
  Register #(.width(4)) register_7 (
    .D(multiplexer_2_out), .en(PCE), .Q(register_7_q), .clk(multiplexer_1_out), .clr(Reset));
  assign {ram_1_data_2, ram_1_data} = RAO_2 ? register_4_q : 8'bz;  // Controlled_Buffer controlled_buffer_4
  assign {ram_1_data_2, ram_1_data} = RBO ? register_5_q : 8'bz;  // Controlled_Buffer controlled_buffer_5
  Adder adder_3 (.a(register_4_q), .b(register_5_q), .out(adder_3_out));  // open: cin, cout
  Multiplexer #(.width(8)) multiplexer_3 (
    .in0(adder_3_out), .in1(subtractor_1_out), .out({ram_1_data_2, ram_1_data}), .sel(LUS), .en(LUO));
  Subtractor subtractor_1 (.a(register_4_q), .b(register_5_q), .out(subtractor_1_out));  // open: bin, bout
  _7_Segment_Display u_7_segment_display_1 (
    .g(n7_segment_rom_1_out_4[3]), .f(n7_segment_rom_1_out_4[2]), .a(n7_segment_rom_1_out_4[1]),
    .b(n7_segment_rom_1_out_4[0]), .e(n7_segment_rom_1_out_4_2[3]), .d(n7_segment_rom_1_out_4_2[2]),
    .c(n7_segment_rom_1_out_4_2[1]), .dp(n7_segment_rom_1_out_4_2[0]));
  Hex_Digit_Display hex_digit_display_1 (.value(register_6_q_2), .dp(1'b1));
  _7_Segment_ROM u_7_segment_rom_1 (
    .IN({register_6_q_2, register_6_q}), .out_2({n7_segment_rom_1_out_2_2, n7_segment_rom_1_out_2}),
    .out_3({n7_segment_rom_1_out_3_2, n7_segment_rom_1_out_3}),
    .out_4({n7_segment_rom_1_out_4_2, n7_segment_rom_1_out_4}));
  _7_Segment_Display u_7_segment_display_2 (
    .g(n7_segment_rom_1_out_2[3]), .f(n7_segment_rom_1_out_2[2]), .a(n7_segment_rom_1_out_2[1]),
    .b(n7_segment_rom_1_out_2[0]), .e(n7_segment_rom_1_out_2_2[3]), .d(n7_segment_rom_1_out_2_2[2]),
    .c(n7_segment_rom_1_out_2_2[1]), .dp(n7_segment_rom_1_out_2_2[0]));
  _7_Segment_Display u_7_segment_display_3 (
    .g(n7_segment_rom_1_out_3[3]), .f(n7_segment_rom_1_out_3[2]), .a(n7_segment_rom_1_out_3[1]),
    .b(n7_segment_rom_1_out_3[0]), .e(n7_segment_rom_1_out_3_2[3]), .d(n7_segment_rom_1_out_3_2[2]),
    .c(n7_segment_rom_1_out_3_2[1]), .dp(n7_segment_rom_1_out_3_2[0]));
  Hex_Digit_Display hex_digit_display_2 (.value(register_6_q), .dp(1'b1));

  // Notes on the sheet:
  //   contents of rom_1 (hex, n*v repeats v):
  //   4 15 e0 c1 0 1
  //   contents of rom_2 (hex, n*v repeats v):
  //   16*102 16*1204 2100 2100 10*0 2005 0 90 0 208 220 10*0 10000 0 10000 0 10000 8008
endmodule

module _7_Segment_ROM (
  input  [7:0] IN,
  output [7:0] out_2,
  output [7:0] out_3,
  output [7:0] out_4
);

  ROM rom_1 (.addr(IN), .data(out_2), .sel(1'b1));
  ROM rom_2 (.addr(IN), .data(out_3), .sel(1'b1));
  ROM rom_3 (.addr(IN), .data(out_4), .sel(1'b1));

  // Notes on the sheet:
  //   Ones
  //   Tens
  //   Hundreds
  //   contents of rom_1 (hex, n*v repeats v):
  //   e7 21 cb 6b 2d 6e ee 23 ef 2f e7 21 cb 6b 2d 6e ee 23 ef 2f e7 21 cb 6b 2d 6e ee 23 ef 2f e7 21 cb
  //   6b 2d 6e ee 23 ef 2f e7 21 cb 6b 2d 6e ee 23 ef 2f e7 21 cb 6b 2d 6e ee 23 ef 2f e7 21 cb 6b 2d 6e
  //   ee 23 ef 2f e7 21 cb 6b 2d 6e ee 23 ef 2f e7 21 cb 6b 2d 6e ee 23 ef 2f e7 21 cb 6b 2d 6e ee 23 ef
  //   2f e7 21 cb 6b 2d 6e ee 23 ef 2f e7 21 cb 6b 2d 6e ee 23 ef 2f e7 21 cb 6b 2d 6e ee 23 ef 2f e7 21
  //   cb 6b 2d 6e ee 23 ef 2f e7 21 cb 6b 2d 6e ee 23 ef 2f e7 21 cb 6b 2d 6e ee 23 ef 2f e7 21 cb 6b 2d
  //   6e ee 23 ef 2f e7 21 cb 6b 2d 6e ee 23 ef 2f e7 21 cb 6b 2d 6e ee 23 ef 2f e7 21 cb 6b 2d 6e ee 23
  //   ef 2f e7 21 cb 6b 2d 6e ee 23 ef 2f e7 21 cb 6b 2d 6e ee 23 ef 2f e7 21 cb 6b 2d 6e ee 23 ef 2f e7
  //   21 cb 6b 2d 6e ee 23 ef 2f e7 21 cb 6b 2d 6e ee 23 ef 2f e7 21 cb 6b 2d 6e
  //   contents of rom_2 (hex, n*v repeats v):
  //   10*0 10*21 10*cb 10*6b 10*2d 10*6e 10*ee 10*23 10*ef 10*2f 10*e7 10*21 10*cb 10*6b 10*2d 10*6e 10*ee
  //   10*23 10*ef 10*2f 10*e7 10*21 10*cb 10*6b 10*2d 6*6e
  //   contents of rom_3 (hex, n*v repeats v):
  //   100*0 100*21 56*cb
endmodule
