// Logisim project BIG+CPU.circ as structural Verilog: 5 circuits, main circuit main
module main (
  input  in_1,
  input  in_2
);

  wire clock_1_out, decoder_1_out0, decoder_1_out1, decoder_2_out0, decoder_2_out1, multiplexer_1_out,
       undriven, undriven_2, undriven_3, undriven_4, undriven_5, undriven_6, undriven_7, undriven_8,
       undriven_9, undriven_10, undriven_11, undriven_16, undriven_17, undriven_18, undriven_19, undriven_20,
       undriven_21;
  wire [3:0] n4_bit_register_1_ou, n4_bit_register_2_ou, n4_bit_register_3_ou, undriven_12, undriven_13;
  wire [7:0] controlled_buffer_1_out, ram_1_data, undriven_14, undriven_15;

  Multiplexer #(.enable("false")) multiplexer_1 (.in0(clock_1_out), .in1(in_2), .out(multiplexer_1_out), .sel(in_1));
  Clock clock_1 (.out(clock_1_out));
  _4_bit_Register u_4_bit_register_1 (
    .i0(undriven_12), .ld(undriven_7), .r0(undriven_6), .en(undriven_8), .ou(n4_bit_register_1_ou));
  _4_bit_Register u_4_bit_register_2 (
    .i0(undriven_13), .ld(undriven_7), .r0(undriven_6), .en(undriven_8), .ou(n4_bit_register_2_ou));
  _4_bit_Register u_4_bit_register_3 (
    .i0(controlled_buffer_1_out[3:0]), .ld(undriven), .r0(undriven_2), .en(1'b1), .ou(n4_bit_register_3_ou));
  assign controlled_buffer_1_out = undriven_4 ? ram_1_data : 8'bz;  // Controlled_Buffer controlled_buffer_1
  RAM #(.addrWidth(4), .bus("separate")) ram_1 (
    .addr(n4_bit_register_3_ou), .din(controlled_buffer_1_out), .data(ram_1_data), .str(undriven_3),
    .sel(undriven_9), .clk(undriven_10), .ld(undriven_5), .clr(undriven_11));
  _8_bit_Register REG_A (
    .i0(controlled_buffer_1_out), .ld(decoder_1_out0), .r0(decoder_2_out0), .en(1'b1), .ou(undriven_14));
  _8_bit_Register REG_B (
    .i0(controlled_buffer_1_out), .ld(decoder_1_out1), .r0(decoder_2_out1), .en(1'b1), .ou(undriven_15));
  ALU alu_1 (
    .in_1(undriven_14), .in_5(controlled_buffer_1_out), .in_2(undriven_15), .in_3(undriven_17),
    .in_4(undriven_16));
  Decoder decoder_1 (.out0(decoder_1_out0), .out1(decoder_1_out1), .sel(undriven_18), .en(undriven_20));
  Decoder decoder_2 (.out0(decoder_2_out0), .out1(decoder_2_out1), .sel(undriven_19), .en(undriven_21));
  // Probe on undriven_20
  // Probe on undriven_18
  // Probe on undriven_21
  // Probe on undriven_19
  // Probe on undriven_16
  // Probe on undriven_17

  // Notes on the sheet:
  //   RAM
  //   Load Decode
  //   Reset Decode
endmodule

module ALU (
  input  [7:0] in_1,
  input  [7:0] in_2,
  input  in_3,
  input  in_4,
  input  [7:0] in_5
);

  wire not_1_out, not_2_out;
  wire [7:0] adder_1_out, controlled_buffer_1_out, controlled_buffer_3_out, subtractor_1_out;

  Adder adder_1 (.a(in_1), .b(in_2), .out(adder_1_out));  // open: cin, cout
  Subtractor subtractor_1 (.a(in_1), .b(in_2), .out(subtractor_1_out));  // open: bin, bout
  not not_1 (not_1_out, in_3);
  assign controlled_buffer_1_out = in_4 ? adder_1_out : 8'bz;  // Controlled_Buffer controlled_buffer_1
  assign in_5 = not_2_out ? controlled_buffer_1_out : 8'bz;  // Controlled_Buffer controlled_buffer_2
  not not_2 (not_2_out, not_1_out);
  assign controlled_buffer_3_out = in_4 ? subtractor_1_out : 8'bz;  // Controlled_Buffer controlled_buffer_3
  assign in_5 = not_1_out ? controlled_buffer_3_out : 8'bz;  // Controlled_Buffer controlled_buffer_4
endmodule

module _8_bit_Register (
  input  [7:0] i0,
  input  [7:0] ou,
  input  ld,
  input  r0,
  input  en
);

  wire [7:0] register_1_q;

  Register register_1 (.D(i0), .en(1'b1), .Q(register_1_q), .clk(ld), .clr(r0));
  assign ou = en ? register_1_q : 8'bz;  // Controlled_Buffer controlled_buffer_1
endmodule

module _4_bit_Register (
  input  [3:0] i0,
  input  ld,
  input  r0,
  input  en,
  output [3:0] ou
);

  wire [3:0] register_1_q;

  Register #(.width(4)) register_1 (.D(i0), .en(1'b1), .Q(register_1_q), .clk(ld), .clr(r0));
  assign ou = en ? register_1_q : 4'bz;  // Controlled_Buffer controlled_buffer_1
endmodule

module PC (
  input  [3:0] i0,
  input  JP,
  input  Ck,
  input  CE,
  output [3:0] Ou
);

  wire and_1_out;
  wire [3:0] adder_1_out, multiplexer_1_out;

  Multiplexer #(.width(4), .enable("false")) multiplexer_1 (
    .in0(adder_1_out), .in1(i0), .out(multiplexer_1_out), .sel(JP));
  and and_1 (and_1_out, Ck, CE);
  Register #(.width(4)) register_1 (.D(multiplexer_1_out), .en(and_1_out), .Q(Ou));  // open: clk, clr
  Adder #(.width(4)) adder_1 (.a(Ou), .b(4'b0001), .out(adder_1_out));  // open: cin, cout
endmodule
