// Logisim project Pipelined Cpu.circ as structural Verilog: 2 circuits, main circuit main
module main (
);

  wire counter_1_carry, counter_2_carry, not_1_out, or_1_out, or_2_out, undriven, undriven_2, undriven_3,
       undriven_4, undriven_5, undriven_6, undriven_7, undriven_8, undriven_9, undriven_10, undriven_11,
       undriven_14, undriven_15, undriven_16, undriven_17;
  wire [0:0] adder_1_cout;
  wire [1:0] undriven_12;
  wire [2:0] undriven_13;
  wire [3:0] n7_segment_controler_1_out_3, n7_segment_controler_1_out_3_2, n7_segment_controler_1_out_4,
       n7_segment_controler_1_out_4_2;
  wire [7:0] adder_1_out, and_1_out, and_2_out, controlled_buffer_1_out, counter_1_q, demultiplexer_1_out0,
       demultiplexer_1_out1, demultiplexer_1_out2, multiplexer_1_out, multiplier_1_out,
       n7_segment_controler_1_out_2, ram_1_data, register_1_q, register_2_q, register_3_q, register_4_q,
       register_5_q, rom_1_data, subtractor_1_out;
  wire [11:8] counter_2_q;
  wire [23:0] rom_2_data;

  assign controlled_buffer_1_out = undriven_3 ? counter_1_q : 8'bz;  // Controlled_Buffer controlled_buffer_1
  assign controlled_buffer_1_out = undriven ? rom_1_data : 8'bz;  // Controlled_Buffer controlled_buffer_2
  Register register_1 (
    .D(controlled_buffer_1_out), .en(undriven_2), .Q(register_1_q), .clk(undriven_16), .clr(undriven_8));
  not not_1 (not_1_out, undriven_16);
  Counter counter_1 (
    .load(undriven_5), .D(register_1_q), .count(undriven_4), .Q(counter_1_q), .carry(counter_1_carry),
    .clk(undriven_16), .clr(or_1_out));
  or or_1 (or_1_out, counter_1_carry, undriven_8, undriven_10);
  Register register_2 (.D(rom_1_data), .en(undriven_6), .Q(register_2_q), .clk(undriven_16), .clr(undriven_8));
  Counter #(.width(4), .max('hf)) counter_2 (
    .load(1'b0), .count(undriven_7), .Q(counter_2_q), .carry(counter_2_carry), .clk(not_1_out), .clr(or_2_out));  // open: D
  or or_2 (or_2_out, counter_2_carry, undriven_8, rom_2_data[23]);
  RAM #(.bus("separate")) ram_1 (
    .addr(register_1_q), .din(demultiplexer_1_out0), .data(ram_1_data), .str(undriven_9), .sel(1'b1),
    .clk(undriven_16), .ld(undriven_11), .clr(undriven_8));
  ROM rom_1 (.addr(register_1_q), .data(rom_1_data), .sel(1'b1));
  ROM #(.addrWidth(12), .dataWidth(24)) rom_2 (.addr({counter_2_q, register_2_q}), .data(rom_2_data), .sel(1'b1));
  Demultiplexer #(.select(2), .width(8), .enable("false")) demultiplexer_1 (
    .out0(demultiplexer_1_out0), .out1(demultiplexer_1_out1), .out2(demultiplexer_1_out2),
    .in(multiplexer_1_out), .sel(undriven_12));  // open: out3
  Multiplexer #(.select(3), .width(8), .enable("false")) multiplexer_1 (
    .in0(register_3_q), .in1(register_4_q), .in2(ram_1_data), .in3(rom_1_data), .in4(adder_1_out),
    .in5(subtractor_1_out), .in6(multiplier_1_out), .out(multiplexer_1_out), .sel(undriven_13));  // open: in7
  Register register_3 (
    .D(demultiplexer_1_out1), .en(undriven_15), .Q(register_3_q), .clk(undriven_16), .clr(undriven_8));
  Register register_4 (
    .D(demultiplexer_1_out2), .en(undriven_14), .Q(register_4_q), .clk(undriven_16), .clr(undriven_8));
  Register register_5 (.D(register_3_q), .en(undriven_17), .Q(register_5_q), .clk(undriven_16), .clr(undriven_8));
  Adder adder_1 (.a(register_3_q), .b(register_4_q), .out(adder_1_out), .cout(adder_1_cout[0]));  // open: cin
  Subtractor subtractor_1 (.a(register_3_q), .b(register_4_q), .out(subtractor_1_out));  // open: bin, bout
  Multiplier multiplier_1 (.a(register_3_q), .b(register_4_q), .out(multiplier_1_out));  // open: cin, cout
  assign and_1_out = multiplexer_1_out & {8{1'b0}};  // AND_Gate and_1, 8 bits wide
  assign and_2_out = subtractor_1_out & {8{1'b0}};  // AND_Gate and_2, 8 bits wide
  _7_Segment_Controler u_7_segment_controler_1 (
    .IN(register_5_q), .out_2(n7_segment_controler_1_out_2),
    .out_3({n7_segment_controler_1_out_3_2, n7_segment_controler_1_out_3}),
    .out_4({n7_segment_controler_1_out_4_2, n7_segment_controler_1_out_4}));
  _7_Segment_Display u_7_segment_display_1 (
    .g(n7_segment_controler_1_out_4[3]), .f(n7_segment_controler_1_out_4[2]),
    .a(n7_segment_controler_1_out_4[1]), .b(n7_segment_controler_1_out_4[0]),
    .e(n7_segment_controler_1_out_4_2[3]), .d(n7_segment_controler_1_out_4_2[2]),
    .c(n7_segment_controler_1_out_4_2[1]), .dp(n7_segment_controler_1_out_4_2[0]));
  _7_Segment_Display u_7_segment_display_2 (
    .g(n7_segment_controler_1_out_3[3]), .f(n7_segment_controler_1_out_3[2]),
    .a(n7_segment_controler_1_out_3[1]), .b(n7_segment_controler_1_out_3[0]),
    .e(n7_segment_controler_1_out_3_2[3]), .d(n7_segment_controler_1_out_3_2[2]),
    .c(n7_segment_controler_1_out_3_2[1]), .dp(n7_segment_controler_1_out_3_2[0]));
  _7_Segment_Display u_7_segment_display_3 (
    .g(n7_segment_controler_1_out_2[3]), .f(n7_segment_controler_1_out_2[2]),
    .a(n7_segment_controler_1_out_2[1]), .b(n7_segment_controler_1_out_2[0]),
    .e(n7_segment_controler_1_out_2[7]), .d(n7_segment_controler_1_out_2[6]),
    .c(n7_segment_controler_1_out_2[5]), .dp(n7_segment_controler_1_out_2[4]));
  // Pins of 1 and 8 bits meet at and_2_out
  // Pins of 1 and 8 bits meet at and_1_out
endmodule

module _7_Segment_Controler (
  input  [7:0] IN,
  output [7:0] out_2,
  output [7:0] out_3,
  output [7:0] out_4
);

  ROM rom_1 (.addr(IN), .data(out_2), .sel(1'b1));
  ROM rom_2 (.addr(IN), .data(out_3), .sel(1'b1));
  ROM rom_3 (.addr(IN), .data(out_4), .sel(1'b1));

  // Notes on the sheet:
  //   Ones
  //   Tens
  //   Hundreds
  //   contents of rom_1 (hex, n*v repeats v):
  //   e7 21 cb 6b 2d 6e ee 23 ef 2f e7 21 cb 6b 2d 6e ee 23 ef 2f e7 21 cb 6b 2d 6e ee 23 ef 2f e7 21 cb
  //   6b 2d 6e ee 23 ef 2f e7 21 cb 6b 2d 6e ee 23 ef 2f e7 21 cb 6b 2d 6e ee 23 ef 2f e7 21 cb 6b 2d 6e
  //   ee 23 ef 2f e7 21 cb 6b 2d 6e ee 23 ef 2f e7 21 cb 6b 2d 6e ee 23 ef 2f e7 21 cb 6b 2d 6e ee 23 ef
  //   2f e7 21 cb 6b 2d 6e ee 23 ef 2f e7 21 cb 6b 2d 6e ee 23 ef 2f e7 21 cb 6b 2d 6e ee 23 ef 2f e7 21
  //   cb 6b 2d 6e ee 23 ef 2f e7 21 cb 6b 2d 6e ee 23 ef 2f e7 21 cb 6b 2d 6e ee 23 ef 2f e7 21 cb 6b 2d
  //   6e ee 23 ef 2f e7 21 cb 6b 2d 6e ee 23 ef 2f e7 21 cb 6b 2d 6e ee 23 ef 2f e7 21 cb 6b 2d 6e ee 23
  //   ef 2f e7 21 cb 6b 2d 6e ee 23 ef 2f e7 21 cb 6b 2d 6e ee 23 ef 2f e7 21 cb 6b 2d 6e ee 23 ef 2f e7
  //   21 cb 6b 2d 6e ee 23 ef 2f e7 21 cb 6b 2d 6e ee 23 ef 2f e7 21 cb 6b 2d 6e
  //   contents of rom_2 (hex, n*v repeats v):
  //   10*0 10*21 10*cb 10*6b 10*2d 10*6e 10*ee 10*23 10*ef 10*2f 10*e7 10*21 10*cb 10*6b 10*2d 10*6e 10*ee
  //   10*23 10*ef 10*2f 10*e7 10*21 10*cb 10*6b 10*2d 6*6e
  //   contents of rom_3 (hex, n*v repeats v):
  //   100*0 100*21 56*cb
endmodule
